// Logisim project Lab1.circ as structural Verilog: 7 circuits, main circuit main
module main (
  output [6:0] out_1
);

  wire and_1_out, and_2_out, and_3_out, AVAILABLE, clock_1_out, clock_2_out, not_2_out, NOTAVAILABLE,
       or_2_out, or_3_out, RAMCLK, RESETRAMADR, RESETROMCOUNTER, ROMCOUNTERFULLCYCLE, SHOWMESSAGE,
       WRITINGCLOCK_out;
  wire [2:0] BTNBUS, contadora5_1_out_4;
  wire [6:0] COLUMNTODISPLAY, ramaddress_1_out_3;
  wire [9:0] KBDBUS, romaddress_1_out_3;
  wire [34:0] LED0, LED6, LED11, LED16, LED21, LED26, LED31, LED36, LED41, LED46, LED51, LED56;

  Button ResetBtn (.out(BTNBUS[0]));
  Clock clock_1 (.out(clock_1_out));
  Button LoadMessage (.out(BTNBUS[1]));
  Keyboard keyboard_1 (.clk(clock_1_out), .re(KBDBUS[9]), .clr(BTNBUS[0]), .avail(AVAILABLE), .data(KBDBUS[6:0]));
  not not_1 (NOTAVAILABLE, AVAILABLE);
  not not_2 (not_2_out, KBDBUS[9]);
  Button u_ShowMessage (.out(BTNBUS[2]));
  DotMatrix #(.matrixcols(60)) dotmatrix_1 (
    .col0(LED56[34:28]), .col1(LED56[27:21]), .col2(LED56[20:14]), .col3(LED56[13:7]), .col4(LED56[6:0]),
    .col5(LED51[34:28]), .col6(LED51[27:21]), .col7(LED51[20:14]), .col8(LED51[13:7]), .col9(LED51[6:0]),
    .col10(LED46[34:28]), .col11(LED46[27:21]), .col12(LED46[20:14]), .col13(LED46[13:7]),
    .col14(LED46[6:0]), .col15(LED41[34:28]), .col16(LED41[27:21]), .col17(LED41[20:14]),
    .col18(LED41[13:7]), .col19(LED41[6:0]), .col20(LED36[34:28]), .col21(LED36[27:21]),
    .col22(LED36[20:14]), .col23(LED36[13:7]), .col24(LED36[6:0]), .col25(LED31[34:28]),
    .col26(LED31[27:21]), .col27(LED31[20:14]), .col28(LED31[13:7]), .col29(LED31[6:0]),
    .col30(LED26[34:28]), .col31(LED26[27:21]), .col32(LED26[20:14]), .col33(LED26[13:7]),
    .col34(LED26[6:0]), .col35(LED21[34:28]), .col36(LED21[27:21]), .col37(LED21[20:14]),
    .col38(LED21[13:7]), .col39(LED21[6:0]), .col40(LED16[34:28]), .col41(LED16[27:21]),
    .col42(LED16[20:14]), .col43(LED16[13:7]), .col44(LED16[6:0]), .col45(LED11[34:28]),
    .col46(LED11[27:21]), .col47(LED11[20:14]), .col48(LED11[13:7]), .col49(LED11[6:0]), .col50(LED6[34:28]),
    .col51(LED6[27:21]), .col52(LED6[20:14]), .col53(LED6[13:7]), .col54(LED6[6:0]), .col55(LED0[34:28]),
    .col56(LED0[27:21]), .col57(LED0[20:14]), .col58(LED0[13:7]), .col59(LED0[6:0]));
  or or_1 (RESETRAMADR, BTNBUS[0], BTNBUS[2]);
  or or_2 (or_2_out, RESETRAMADR, not_2_out);
  and and_1 (and_1_out, NOTAVAILABLE, SHOWMESSAGE);
  Clock clock_2 (.out(clock_2_out));
  or or_3 (or_3_out, AVAILABLE, RESETROMCOUNTER);
  and and_2 (and_2_out, NOTAVAILABLE, clock_2_out);
  RamAddress ramaddress_1 (.RESET(or_2_out), .CLK(RAMCLK), .out_3(ramaddress_1_out_3));
  and and_3 (and_3_out, AVAILABLE, KBDBUS[9]);
  RAM #(.addrWidth(7), .clearpin("true"), .dataWidth(7)) ram_1 (
    .addr(ramaddress_1_out_3), .we(and_3_out), .oe(NOTAVAILABLE), .clk(RAMCLK), .din(KBDBUS[6:0]),
    .dout(out_1), .clr(BTNBUS[0]));
  ContadorA5 contadora5_1 (
    .CLK(and_2_out), .X(and_1_out), .RESET(or_3_out), .out_4(contadora5_1_out_4), .Z(ROMCOUNTERFULLCYCLE));
  D_Flip_Flop d_ff_1 (.D(1'b1), .clk(BTNBUS[1]), .Q(KBDBUS[9]), .reset(BTNBUS[0]));  // open: Qn, preset
  or or_4 (RESETROMCOUNTER, BTNBUS[0], BTNBUS[1], BTNBUS[2]);
  ROM #(.addrWidth(10), .dataWidth(7)) rom_1 (.addr(romaddress_1_out_3), .data(COLUMNTODISPLAY));
  RomAddress romaddress_1 (.DIN(out_1), .COUNT(contadora5_1_out_4), .out_3(romaddress_1_out_3));
  Clock WRITINGCLOCK (.out(WRITINGCLOCK_out));
  D_Flip_Flop d_ff_2 (.D(1'b1), .clk(BTNBUS[2]), .Q(SHOWMESSAGE), .reset(BTNBUS[0]));  // open: Qn, preset
  Multiplexer multiplexer_1 (.in0(ROMCOUNTERFULLCYCLE), .in1(WRITINGCLOCK_out), .out(RAMCLK), .sel(AVAILABLE));
  pantalla pantalla_1 (
    .DIN(COLUMNTODISPLAY), .RESET(BTNBUS[0]), .LED0(LED0), .LED6(LED6), .LED11(LED11), .LED16(LED16),
    .LED21(LED21), .LED26(LED26), .LED31(LED31), .LED36(LED36), .LED41(LED41), .LED46(LED46), .LED51(LED51),
    .LED56(LED56));

  // Other names for the same wires on the sheet: KBDBUS[8:7] = {BTNBUS[0], AVAILABLE}; OTHERRESETS = BTNBUS[0];
  //   RESETBTNSIGNAL = BTNBUS[0]; RESETKBD = BTNBUS[0]; RESETRAMVALUES = BTNBUS[0]; LOADMESSAGEBTNSIGNAL = BTNBUS[1];
  //   SHOWMESSAGEBTNSIGNAL = BTNBUS[2]; KDBDATA[6:0] = KBDBUS[6:0]; KBDENABLE = KBDBUS[9]; RAMOUTPUT[6:0] = out_1

  // Notes on the sheet:
  //   * Limpiar Ram
  //   Señales del teclado
  //   * Limpiar Teclado
  //   * Limpiar Flip Flops
  //   * Limpiar Pantalla
  //   Comportamiento de la ram
  //   Comportamiento de la rom
  //   Funcionamiento cuando hacemos click al Reset
  //   Comportamiento del reset de la direccion de la ram
  //   Señales de los botones
  //   Comportamiento para resetear el contador de la rom
  //   Funcionamiento cuando iniciamos el cargado del mensaje en la RAM
  //   Circuito de la pantalla
  //   Controlador de reloj de la ram
  //   por completar un ciclo en el contador de la rom
  //   El reloj de lectura corresponde al flanco de subida generado
  //   Funcionamiento cuando iniciamos a mostrar el mensaje en la pantalla
endmodule

module ten_registers (
  input  [6:0] DIN,
  input  CLK,
  input  RESET,
  output [6:0] DO1,
  output [6:0] DO2,
  output [6:0] DO3,
  output [6:0] DO4,
  output [6:0] DO5,
  output [6:0] DO6,
  output [6:0] DO7,
  output [6:0] DO8,
  output [6:0] DO9,
  output [6:0] DO10
);

  Register #(.width(7)) register_1 (.D(DIN), .clk(CLK), .Q(DO1), .clr(RESET));  // open: en
  Register #(.width(7)) register_2 (.D(DO1), .clk(CLK), .Q(DO2), .clr(RESET));  // open: en
  Register #(.width(7)) register_3 (.D(DO2), .clk(CLK), .Q(DO3), .clr(RESET));  // open: en
  Register #(.width(7)) register_4 (.D(DO3), .clk(CLK), .Q(DO4), .clr(RESET));  // open: en
  Register #(.width(7)) register_5 (.D(DO4), .clk(CLK), .Q(DO5), .clr(RESET));  // open: en
  Register #(.width(7)) register_6 (.D(DO5), .clk(CLK), .Q(DO6), .clr(RESET));  // open: en
  Register #(.width(7)) register_7 (.D(DO6), .clk(CLK), .Q(DO7), .clr(RESET));  // open: en
  Register #(.width(7)) register_8 (.D(DO7), .clk(CLK), .Q(DO8), .clr(RESET));  // open: en
  Register #(.width(7)) register_9 (.D(DO8), .clk(CLK), .Q(DO9), .clr(RESET));  // open: en
  Register #(.width(7)) register_10 (.D(DO9), .clk(CLK), .Q(DO10), .clr(RESET));  // open: en
endmodule

module pantalla (
  input  [6:0] DIN,
  input  RESET,
  output [34:0] LED0,
  output [34:0] LED6,
  output [34:0] LED11,
  output [34:0] LED16,
  output [34:0] LED21,
  output [34:0] LED26,
  output [34:0] LED31,
  output [34:0] LED36,
  output [34:0] LED41,
  output [34:0] LED46,
  output [34:0] LED51,
  output [34:0] LED56
);

  wire CLK;

  Clock clock_1 (.out(CLK));
  ten_registers ten_registers_1 (
    .DIN(DIN), .CLK(CLK), .RESET(RESET), .DO1(LED0[6:0]), .DO2(LED0[13:7]), .DO3(LED0[20:14]),
    .DO4(LED0[27:21]), .DO5(LED0[34:28]), .DO6(LED6[6:0]), .DO7(LED6[13:7]), .DO8(LED6[20:14]),
    .DO9(LED6[27:21]), .DO10(LED6[34:28]));
  ten_registers ten_registers_2 (
    .DIN(LED6[34:28]), .CLK(CLK), .RESET(RESET), .DO1(LED11[6:0]), .DO2(LED11[13:7]), .DO3(LED11[20:14]),
    .DO4(LED11[27:21]), .DO5(LED11[34:28]), .DO6(LED16[6:0]), .DO7(LED16[13:7]), .DO8(LED16[20:14]),
    .DO9(LED16[27:21]), .DO10(LED16[34:28]));
  ten_registers ten_registers_3 (
    .DIN(LED16[34:28]), .CLK(CLK), .RESET(RESET), .DO1(LED21[6:0]), .DO2(LED21[13:7]), .DO3(LED21[20:14]),
    .DO4(LED21[27:21]), .DO5(LED21[34:28]), .DO6(LED26[6:0]), .DO7(LED26[13:7]), .DO8(LED26[20:14]),
    .DO9(LED26[27:21]), .DO10(LED26[34:28]));
  ten_registers ten_registers_4 (
    .DIN(LED26[34:28]), .CLK(CLK), .RESET(RESET), .DO1(LED31[6:0]), .DO2(LED31[13:7]), .DO3(LED31[20:14]),
    .DO4(LED31[27:21]), .DO5(LED31[34:28]), .DO6(LED36[6:0]), .DO7(LED36[13:7]), .DO8(LED36[20:14]),
    .DO9(LED36[27:21]), .DO10(LED36[34:28]));
  ten_registers ten_registers_5 (
    .DIN(LED36[34:28]), .CLK(CLK), .RESET(RESET), .DO1(LED41[6:0]), .DO2(LED41[13:7]), .DO3(LED41[20:14]),
    .DO4(LED41[27:21]), .DO5(LED41[34:28]), .DO6(LED46[6:0]), .DO7(LED46[13:7]), .DO8(LED46[20:14]),
    .DO9(LED46[27:21]), .DO10(LED46[34:28]));
  ten_registers ten_registers_6 (
    .DIN(LED46[34:28]), .CLK(CLK), .RESET(RESET), .DO1(LED51[6:0]), .DO2(LED51[13:7]), .DO3(LED51[20:14]),
    .DO4(LED51[27:21]), .DO5(LED51[34:28]), .DO6(LED56[6:0]), .DO7(LED56[13:7]), .DO8(LED56[20:14]),
    .DO9(LED56[27:21]), .DO10(LED56[34:28]));
endmodule

module ContadorA5 (
  input  CLK,
  input  X,
  input  RESET,
  output [2:0] out_4,
  output Z
);

  wire and_1_out, and_2_out, and_3_out, and_4_out, and_5_out, comparator_1_eq, NotQ0, NotQ1, NotQ2, or_1_out;

  and and_1 (and_1_out, X, NotQ1);
  and and_2 (and_2_out, X, NotQ2);
  and and_3 (and_3_out, out_4[0], X, NotQ2);
  and and_4 (and_4_out, X, out_4[0], out_4[1], NotQ2);
  and and_5 (and_5_out, X, out_4[0], NotQ1);
  or or_1 (or_1_out, and_1_out, and_2_out);
  J_K_Flip_Flop j_k_ff_1 (
    .J(or_1_out), .K(or_1_out), .clk(CLK), .Q(out_4[0]), .Qn(NotQ0), .reset(RESET));  // open: preset
  J_K_Flip_Flop j_k_ff_2 (
    .J(and_3_out), .K(and_3_out), .clk(CLK), .Q(out_4[1]), .Qn(NotQ1), .reset(RESET));  // open: preset
  J_K_Flip_Flop j_k_ff_3 (
    .J(and_4_out), .K(and_5_out), .clk(CLK), .Q(out_4[2]), .Qn(NotQ2), .reset(RESET));  // open: preset
  Comparator #(.width(3)) comparator_1 (.a(out_4), .b(3'b101), .eq(comparator_1_eq));  // open: gt, lt
  D_Flip_Flop d_ff_1 (.D(comparator_1_eq), .clk(CLK), .Q(Z), .reset(RESET));  // open: Qn, preset

  // Other names for the same wires on the sheet: Q0 = out_4[0]; Q1 = out_4[1]; Q2 = out_4[2]

  // Notes on the sheet:
  //   SALIDA Q0
  //   SALIDA Q1
  //   SALIDA Q2
endmodule

module ContadorA6 (
  input  CLK,
  input  X,
  input  RESET,
  output Z,
  output [2:0] out_5
);

  wire and_1_out, and_2_out, and_3_out, and_4_out, and_5_out, and_6_out, and_7_out, comparator_1_eq, NotQ0,
       NotQ1, NotQ2, or_1_out, or_2_out;

  and and_1 (and_1_out, NotQ1, X);
  and and_2 (and_2_out, NotQ2, X);
  and and_3 (and_3_out, X, out_5[2]);
  and and_4 (and_4_out, NotQ2, out_5[0], X);
  and and_5 (and_5_out, NotQ1, out_5[0], X);
  and and_6 (and_6_out, X, out_5[0], out_5[1], NotQ2);
  and and_7 (and_7_out, X, out_5[1], NotQ0);
  or or_1 (or_1_out, and_1_out, and_2_out);
  or or_2 (or_2_out, and_3_out, and_4_out);
  J_K_Flip_Flop j_k_ff_1 (
    .J(or_1_out), .K(or_1_out), .clk(CLK), .Q(out_5[0]), .Qn(NotQ0), .reset(RESET));  // open: preset
  J_K_Flip_Flop j_k_ff_2 (
    .J(and_5_out), .K(or_2_out), .clk(CLK), .Q(out_5[1]), .Qn(NotQ1), .reset(RESET));  // open: preset
  J_K_Flip_Flop j_k_ff_3 (
    .J(and_6_out), .K(and_7_out), .clk(CLK), .Q(out_5[2]), .Qn(NotQ2), .reset(RESET));  // open: preset
  Comparator #(.width(3)) comparator_1 (.a(out_5), .b(3'b110), .eq(comparator_1_eq));  // open: gt, lt
  D_Flip_Flop d_ff_1 (.D(comparator_1_eq), .clk(or_2_out), .Q(Z));  // open: Qn, preset, reset

  // Other names for the same wires on the sheet: Q0 = out_5[0]; Q1 = out_5[1]; Q2 = out_5[2]

  // Notes on the sheet:
  //   SALIDA Q1
  //   SALIDA Q2
endmodule

module RamAddress (
  input  RESET,
  input  CLK,
  output [6:0] out_3
);

  Counter #(.max('h7f), .width(7)) counter_1 (.clr(RESET), .clk(CLK), .Q(out_3));  // open: load, up, count, D, carry
endmodule

module RomAddress (
  input  [6:0] DIN,
  input  [2:0] COUNT,
  output [9:0] out_3
);

  wire comparator_1_eq;
  wire [6:0] multiplexer_1_out, multiplier_1_out, subtractor_1_out;

  Comparator #(.width(7)) comparator_1 (.a(DIN), .b({7{1'b0}}), .eq(comparator_1_eq));  // open: gt, lt
  Multiplexer #(.width(7)) multiplexer_1 (.in0(DIN), .in1(7'b0100000), .out(multiplexer_1_out), .sel(comparator_1_eq));
  Subtractor #(.width(7)) subtractor_1 (
    .a(multiplexer_1_out), .b(7'b0100000), .out(subtractor_1_out));  // open: bin, bout
  Multiplier #(.width(7)) multiplier_1 (
    .a(subtractor_1_out), .b(7'b0000110), .out(multiplier_1_out));  // open: cin, cout
  Adder #(.width(7)) adder_1 (.a(multiplier_1_out), .b({4'b0000, COUNT}), .out(out_3[6:0]));  // open: cin, cout

  assign out_3[9:7] = 3'b000;
endmodule
